// Logisim project P0.circ as structural Verilog
module CRC (
  input  [7:0] initial_data,
  input  [3:0] divisor,
  output [10:0] out_3
);

  wire [2:0] n4bit_mod2divsor_1_out_3, n4bit_mod2divsor_2_out_3, n4bit_mod2divsor_3_out_3,
       n4bit_mod2divsor_4_out_3, n4bit_mod2divsor_5_out_3, n4bit_mod2divsor_6_out_3, n4bit_mod2divsor_7_out_3;

  _4bit_mod2divsor u_4bit_mod2divsor_1 (.in_1(initial_data[7:4]), .in_2(divisor), .out_3(n4bit_mod2divsor_1_out_3));
  _4bit_mod2divsor u_4bit_mod2divsor_2 (
    .in_1({n4bit_mod2divsor_1_out_3, initial_data[3]}), .in_2(divisor), .out_3(n4bit_mod2divsor_2_out_3));
  _4bit_mod2divsor u_4bit_mod2divsor_3 (
    .in_1({n4bit_mod2divsor_2_out_3, initial_data[2]}), .in_2(divisor), .out_3(n4bit_mod2divsor_3_out_3));
  _4bit_mod2divsor u_4bit_mod2divsor_4 (
    .in_1({n4bit_mod2divsor_3_out_3, initial_data[1]}), .in_2(divisor), .out_3(n4bit_mod2divsor_4_out_3));
  _4bit_mod2divsor u_4bit_mod2divsor_5 (
    .in_1({n4bit_mod2divsor_4_out_3, initial_data[0]}), .in_2(divisor), .out_3(n4bit_mod2divsor_5_out_3));
  _4bit_mod2divsor u_4bit_mod2divsor_6 (
    .in_1({n4bit_mod2divsor_5_out_3, 1'b0}), .in_2(divisor), .out_3(n4bit_mod2divsor_6_out_3));
  _4bit_mod2divsor u_4bit_mod2divsor_7 (
    .in_1({n4bit_mod2divsor_6_out_3, 1'b0}), .in_2(divisor), .out_3(n4bit_mod2divsor_7_out_3));
  _4bit_mod2divsor u_4bit_mod2divsor_8 (.in_1({n4bit_mod2divsor_7_out_3, 1'b0}), .in_2(divisor), .out_3(out_3[2:0]));

  assign out_3[10:3] = initial_data;

  // Other names for the same wires on the sheet: O1[2:0] = out_3[2:0]; I2[3:0] = divisor; I1[7:0] = initial_data

  // Notes on the sheet:
  //   除数为四位，原数据帧为8位的CRC校验码计算电路
endmodule

module _4bit_mod2divsor (
  input  [3:0] in_1,
  input  [3:0] in_2,
  output [2:0] out_3
);

  wire [3:0] xor_1_out;

  assign xor_1_out = in_1 ^ in_2;  // XOR_Gate xor_1, 4 bits wide
  Multiplexer #(.width(3)) multiplexer_1 (
    .in0(in_1[2:0]), .in1(xor_1_out[2:0]), .out(out_3), .sel(in_1[3]));  // open: en

  // Other names for the same wires on the sheet: _1st_bit = in_1[3]; initial[2:0] = in_1[2:0]

  // Notes on the sheet:
  //   4位的mod2除法器
endmodule

module alu (
  input  [3:0] in_1,
  input  [3:0] in_2,
  input  [1:0] in_3,
  output [3:0] out_4
);

  wire [3:0] tunnel, tunnel_t, tunnel_t_t, tunnel_t_t_t;

  Adder #(.width(4)) adder_1 (.a(in_1), .b(in_2), .out(tunnel_t));  // open: cin, cout
  Subtractor #(.width(4)) subtractor_1 (.a(in_1), .b(in_2), .out(tunnel_t_t));  // open: bin, bout
  assign tunnel = in_1 & in_2;  // AND_Gate and_1, 4 bits wide
  assign tunnel_t_t_t = in_1 | in_2;  // OR_Gate or_1, 4 bits wide
  Multiplexer #(.select(2), .width(4)) multiplexer_1 (
    .in0(tunnel_t), .in1(tunnel_t_t), .in2(tunnel), .in3(tunnel_t_t_t), .out(out_4), .sel(in_3));  // open: en

  // Other names for the same wires on the sheet: A[3:0] = in_1; B[3:0] = in_2; op[1:0] = in_3

  // Notes on the sheet:
  //   四位的ALU
endmodule

module grf (
  input  [4:0] in_1,
  input  in_2,
  input  in_3,
  input  in_4,
  input  [4:0] in_5,
  input  [4:0] in_6,
  input  [31:0] in_7,
  output [31:0] out_8,
  output [31:0] out_9
);

  wire _1_t, _2_t, _3_t, _4_t, _5_t, _6_t, _7_t, _8_t, _9_t, _10_t, _11_t, _12_t, _13_t, _14_t, _15_t, _16_t,
       _17_t, _18_t, _19_t, _20_t, _21_t, _22_t, _23_t, _24_t, _25_t, _26_t, _27_t, _28_t, _29_t, _30_t,
       _31_t;
  wire [31:0] _0, _1, _2, _3, _4, _5, _6, _7, _8, _9, _10, _11, _12, _13, _14, _15, _16, _17, _18, _19, _20,
       _21, _22, _23, _24, _25, _26, _27, _28, _29, _30, _31, in_1_t, in_2_t, in_3_t, in_4_t, in_5_t, in_6_t,
       in_7_t, in_8, in_9, in_10, in_11, in_12, in_13, in_14, in_15, in_16, in_17, in_18, in_19, in_20,
       in_21, in_22, in_23, in_24, in_25, in_26, in_27, in_28, in_29, in_30, in_31;

  _2_5bit_equal u_2_5bit_equal_1 (.in_1(5'b00001), .in_2(in_6), .out_3(_1_t));
  _2_5bit_equal u_2_5bit_equal_2 (.in_1(5'b00101), .in_2(in_6), .out_3(_5_t));
  _2_5bit_equal u_2_5bit_equal_3 (.in_1(5'b01001), .in_2(in_6), .out_3(_9_t));
  _2_5bit_equal u_2_5bit_equal_4 (.in_1(5'b01101), .in_2(in_6), .out_3(_13_t));
  _2_5bit_equal u_2_5bit_equal_5 (.in_1(5'b10001), .in_2(in_6), .out_3(_17_t));
  _2_5bit_equal u_2_5bit_equal_6 (.in_1(5'b10101), .in_2(in_6), .out_3(_21_t));
  _2_5bit_equal u_2_5bit_equal_7 (.in_1(5'b11001), .in_2(in_6), .out_3(_25_t));
  _2_5bit_equal u_2_5bit_equal_8 (.in_1(5'b11101), .in_2(in_6), .out_3(_29_t));
  Register #(.width(32)) u__0 (.D({32{1'b0}}), .Q(_0), .clk(in_2), .clr(in_3));  // open: en
  Register #(.width(32)) u__10 (.D(in_10), .en(_10_t), .Q(_10), .clk(in_2), .clr(in_3));
  Register #(.width(32)) u__20 (.D(in_20), .en(_20_t), .Q(_20), .clk(in_2), .clr(in_3));
  _2_5bit_equal u_2_5bit_equal_9 (.in_1(5'b00010), .in_2(in_6), .out_3(_2_t));
  _2_5bit_equal u_2_5bit_equal_10 (.in_1(5'b00110), .in_2(in_6), .out_3(_6_t));
  _2_5bit_equal u_2_5bit_equal_11 (.in_1(5'b01010), .in_2(in_6), .out_3(_10_t));
  _2_5bit_equal u_2_5bit_equal_12 (.in_1(5'b01110), .in_2(in_6), .out_3(_14_t));
  _2_5bit_equal u_2_5bit_equal_13 (.in_1(5'b10010), .in_2(in_6), .out_3(_18_t));
  _2_5bit_equal u_2_5bit_equal_14 (.in_1(5'b10110), .in_2(in_6), .out_3(_22_t));
  _2_5bit_equal u_2_5bit_equal_15 (.in_1(5'b11010), .in_2(in_6), .out_3(_26_t));
  _2_5bit_equal u_2_5bit_equal_16 (.in_1(5'b11110), .in_2(in_6), .out_3(_30_t));
  _2_5bit_equal u_2_5bit_equal_17 (.in_1(5'b00011), .in_2(in_6), .out_3(_3_t));
  _2_5bit_equal u_2_5bit_equal_18 (.in_1(5'b00111), .in_2(in_6), .out_3(_7_t));
  _2_5bit_equal u_2_5bit_equal_19 (.in_1(5'b01011), .in_2(in_6), .out_3(_11_t));
  _2_5bit_equal u_2_5bit_equal_20 (.in_1(5'b01111), .in_2(in_6), .out_3(_15_t));
  _2_5bit_equal u_2_5bit_equal_21 (.in_1(5'b10011), .in_2(in_6), .out_3(_19_t));
  _2_5bit_equal u_2_5bit_equal_22 (.in_1(5'b10111), .in_2(in_6), .out_3(_23_t));
  _2_5bit_equal u_2_5bit_equal_23 (.in_1(5'b11011), .in_2(in_6), .out_3(_27_t));
  _2_5bit_equal u_2_5bit_equal_24 (.in_1({5{1'b1}}), .in_2(in_6), .out_3(_31_t));
  Register #(.width(32)) u__1 (.D(in_1_t), .en(_1_t), .Q(_1), .clk(in_2), .clr(in_3));
  Register #(.width(32)) u__11 (.D(in_11), .en(_11_t), .Q(_11), .clk(in_2), .clr(in_3));
  Register #(.width(32)) u__21 (.D(in_21), .en(_21_t), .Q(_21), .clk(in_2), .clr(in_3));
  Register #(.width(32)) u__2 (.D(in_2_t), .en(_2_t), .Q(_2), .clk(in_2), .clr(in_3));
  Register #(.width(32)) u__12 (.D(in_12), .en(_12_t), .Q(_12), .clk(in_2), .clr(in_3));
  Register #(.width(32)) u__22 (.D(in_22), .en(_22_t), .Q(_22), .clk(in_2), .clr(in_3));
  _2_5bit_equal u_2_5bit_equal_25 (.in_1(5'b00100), .in_2(in_6), .out_3(_4_t));
  _2_5bit_equal u_2_5bit_equal_26 (.in_1(5'b01000), .in_2(in_6), .out_3(_8_t));
  _2_5bit_equal u_2_5bit_equal_27 (.in_1(5'b01100), .in_2(in_6), .out_3(_12_t));
  _2_5bit_equal u_2_5bit_equal_28 (.in_1(5'b10000), .in_2(in_6), .out_3(_16_t));
  _2_5bit_equal u_2_5bit_equal_29 (.in_1(5'b10100), .in_2(in_6), .out_3(_20_t));
  _2_5bit_equal u_2_5bit_equal_30 (.in_1(5'b11000), .in_2(in_6), .out_3(_24_t));
  _2_5bit_equal u_2_5bit_equal_31 (.in_1(5'b11100), .in_2(in_6), .out_3(_28_t));
  Register #(.width(32)) u__3 (.D(in_3_t), .en(_3_t), .Q(_3), .clk(in_2), .clr(in_3));
  Register #(.width(32)) u__13 (.D(in_13), .en(_13_t), .Q(_13), .clk(in_2), .clr(in_3));
  Register #(.width(32)) u__23 (.D(in_23), .en(_23_t), .Q(_23), .clk(in_2), .clr(in_3));
  Register #(.width(32)) u__4 (.D(in_4_t), .en(_4_t), .Q(_4), .clk(in_2), .clr(in_3));
  Register #(.width(32)) u__14 (.D(in_14), .en(_14_t), .Q(_14), .clk(in_2), .clr(in_3));
  Register #(.width(32)) u__24 (.D(in_24), .en(_24_t), .Q(_24), .clk(in_2), .clr(in_3));
  Register #(.width(32)) u__5 (.D(in_5_t), .en(_5_t), .Q(_5), .clk(in_2), .clr(in_3));
  Register #(.width(32)) u__15 (.D(in_15), .en(_15_t), .Q(_15), .clk(in_2), .clr(in_3));
  Register #(.width(32)) u__25 (.D(in_25), .en(_25_t), .Q(_25), .clk(in_2), .clr(in_3));
  Multiplexer #(.select(5), .width(32)) multiplexer_1 (
    .in0(_0), .in1(_1), .in2(_2), .in3(_3), .in4(_4), .in5(_5), .in6(_6), .in7(_7), .in8(_8), .in9(_9),
    .in10(_10), .in11(_11), .in12(_12), .in13(_13), .in14(_14), .in15(_15), .in16(_16), .in17(_17),
    .in18(_18), .in19(_19), .in20(_20), .in21(_21), .in22(_22), .in23(_23), .in24(_24), .in25(_25),
    .in26(_26), .in27(_27), .in28(_28), .in29(_29), .in30(_30), .in31(_31), .out(out_8), .sel(in_1));  // open: en
  Multiplexer #(.select(5), .width(32)) multiplexer_2 (
    .in0(_0), .in1(_1), .in2(_2), .in3(_3), .in4(_4), .in5(_5), .in6(_6), .in7(_7), .in8(_8), .in9(_9),
    .in10(_10), .in11(_11), .in12(_12), .in13(_13), .in14(_14), .in15(_15), .in16(_16), .in17(_17),
    .in18(_18), .in19(_19), .in20(_20), .in21(_21), .in22(_22), .in23(_23), .in24(_24), .in25(_25),
    .in26(_26), .in27(_27), .in28(_28), .in29(_29), .in30(_30), .in31(_31), .out(out_9), .sel(in_5));  // open: en
  Register #(.width(32)) u__6 (.D(in_6_t), .en(_6_t), .Q(_6), .clk(in_2), .clr(in_3));
  Register #(.width(32)) u__16 (.D(in_16), .en(_16_t), .Q(_16), .clk(in_2), .clr(in_3));
  Register #(.width(32)) u__26 (.D(in_26), .en(_26_t), .Q(_26), .clk(in_2), .clr(in_3));
  Register #(.width(32)) u__7 (.D(in_7_t), .en(_7_t), .Q(_7), .clk(in_2), .clr(in_3));
  Register #(.width(32)) u__17 (.D(in_17), .en(_17_t), .Q(_17), .clk(in_2), .clr(in_3));
  Register #(.width(32)) u__27 (.D(in_27), .en(_27_t), .Q(_27), .clk(in_2), .clr(in_3));
  Register #(.width(32)) u__8 (.D(in_8), .en(_8_t), .Q(_8), .clk(in_2), .clr(in_3));
  Register #(.width(32)) u__18 (.D(in_18), .en(_18_t), .Q(_18), .clk(in_2), .clr(in_3));
  Register #(.width(32)) u__28 (.D(in_28), .en(_28_t), .Q(_28), .clk(in_2), .clr(in_3));
  Register #(.width(32)) u__9 (.D(in_9), .en(_9_t), .Q(_9), .clk(in_2), .clr(in_3));
  Register #(.width(32)) u__19 (.D(in_19), .en(_19_t), .Q(_19), .clk(in_2), .clr(in_3));
  Register #(.width(32)) u__29 (.D(in_29), .en(_29_t), .Q(_29), .clk(in_2), .clr(in_3));
  Demultiplexer #(.select(5), .width(32)) demultiplexer_1 (
    .out1(in_1_t), .out2(in_2_t), .out3(in_3_t), .out4(in_4_t), .out5(in_5_t), .out6(in_6_t), .out7(in_7_t),
    .out8(in_8), .out9(in_9), .out10(in_10), .out11(in_11), .out12(in_12), .out13(in_13), .out14(in_14),
    .out15(in_15), .out16(in_16), .out17(in_17), .out18(in_18), .out19(in_19), .out20(in_20), .out21(in_21),
    .out22(in_22), .out23(in_23), .out24(in_24), .out25(in_25), .out26(in_26), .out27(in_27), .out28(in_28),
    .out29(in_29), .out30(in_30), .out31(in_31), .in(in_7), .sel(in_6), .en(in_4));  // open: out0
  Register #(.width(32)) u__30 (.D(in_30), .en(_30_t), .Q(_30), .clk(in_2), .clr(in_3));
  Register #(.width(32)) u__31 (.D(in_31), .en(_31_t), .Q(_31), .clk(in_2), .clr(in_3));

  // Other names for the same wires on the sheet: A1[4:0] = in_1; A2[4:0] = in_5; A3[4:0] = in_6; clk = in_2;
  //   RD1[31:0] = out_8; RD2[31:0] = out_9; reset = in_3; WD[31:0] = in_7; WE = in_4
endmodule

module _2_5bit_equal (
  input  [4:0] in_1,
  input  [4:0] in_2,
  output out_3
);

  Comparator #(.width(5), .mode("unsigned")) comparator_1 (.a(in_1), .b(in_2), .eq(out_3));  // open: gt, lt
endmodule

module fsm (
  input  in_1,
  input  [1:0] in_2,
  output out_3
);

  wire and_1_out, and_2_out, and_3_out, and_4_out, and_5_out, and_6_out, and_7_out, and_8_out, clock_1_out,
       not_1_out, not_2_out, not_3_out, not_4_out, not_5_out, not_6_out, not_7_out, not_8_out, not_9_out,
       not_10_out, not_11_out, not_12_out, not_13_out, not_14_out, not_15_out, not_16_out, not_17_out,
       not_18_out, or_1_out, or_2_out, register_1_q, S0, S1;

  and and_1 (and_1_out, S0, not_1_out, not_2_out);
  not not_1 (not_1_out, S1);
  not not_2 (not_2_out, in_2[0]);
  not not_3 (not_3_out, S0);
  and and_2 (and_2_out, not_3_out, S1, not_4_out);
  not not_4 (not_4_out, in_2[0]);
  not not_5 (not_5_out, S0);
  not not_6 (not_6_out, S1);
  and and_3 (and_3_out, not_5_out, not_6_out, in_2[0], not_7_out);
  not not_7 (not_7_out, in_2[1]);
  and and_4 (and_4_out, S0, S1, in_2[0], not_8_out);
  not not_8 (not_8_out, in_2[1]);
  and and_5 (and_5_out, S0, not_9_out, not_10_out);
  not not_9 (not_9_out, S1);
  not not_10 (not_10_out, in_2[1]);
  not not_11 (not_11_out, S0);
  and and_6 (and_6_out, not_11_out, S1, not_12_out);
  not not_12 (not_12_out, in_2[1]);
  not not_13 (not_13_out, S1);
  and and_7 (and_7_out, S0, not_13_out, not_14_out, in_2[1]);
  not not_14 (not_14_out, in_2[0]);
  not not_15 (not_15_out, S0);
  and and_8 (and_8_out, not_15_out, S1, not_16_out, in_2[1]);
  not not_16 (not_16_out, in_2[0]);
  not not_17 (not_17_out, in_1);
  Register #(.width(1)) register_1 (.D(in_1), .Q(register_1_q), .clk(clock_1_out), .clr(not_17_out));  // open: en
  or or_1 (or_1_out, and_1_out, and_2_out, and_3_out, and_4_out);
  or or_2 (or_2_out, and_5_out, and_6_out, and_7_out, and_8_out);
  Register #(.width(1)) u_S0 (.D(or_1_out), .Q(S0), .clk(clock_1_out), .clr(register_1_q));  // open: en
  Clock clock_1 (.out(clock_1_out));
  Register #(.width(1)) u_S1 (.D(or_2_out), .Q(S1), .clk(clock_1_out), .clr(register_1_q));  // open: en
  not not_18 (not_18_out, in_2[0]);
  and and_9 (out_3, S0, S1, not_18_out);

  // Other names for the same wires on the sheet: In0 = in_2[0]; In1 = in_2[1]
endmodule
