// Logisim project P3.circ as structural Verilog: 6 circuits, main circuit main
module main (
  input  Reset,
  output [31:0] Instr,
  output RegWrite,
  output [4:0] RegAddr,
  output [31:0] RegData,
  output MemWrite,
  output [4:0] MemAddr,
  output [31:0] MemData
);

  wire alu_1_equal, clk, controller_1_alusrc, controller_1_dtorf, controller_1_npcsel, controller_1_regdst;
  wire [1:0] controller_1__00_zero_ext_01_sign_ext_10_move_to_hi;
  wire [2:0] controller_1__000_add_001sub_010or_011tohi;
  wire [31:0] alu_1_o, ext_1_out_3, ifu_1_out_5, multiplexer_2_out, ram_1_data, rf_1_oa;

  Clock clock_1 (.out(clk));
  // Probe on ifu_1_out_5
  // Probe on Instr
  IFU ifu_1 (
    .instr(Instr), .clk(clk), .reset(Reset), .offset(ext_1_out_3), .NpcSel(controller_1_npcsel),
    .out_5(ifu_1_out_5));
  // Probe on RegData
  Multiplexer #(.width(5), .enable("false")) multiplexer_1 (
    .in0(Instr[20:16]), .in1(Instr[15:11]), .out(RegAddr), .sel(controller_1_regdst));
  RF rf_1 (
    .A2(Instr[20:16]), .A3(RegAddr), .A1(Instr[25:21]), .WD(RegData), .clk(clk), .reset(Reset), .OA(rf_1_oa),
    .WE(RegWrite), .OB(MemData));
  EXT ext_1 (
    .in_2(Instr[15:0]), .out_3(ext_1_out_3),
    ._0_zero_1_sign(controller_1__00_zero_ext_01_sign_ext_10_move_to_hi));
  Controller controller_1 (
    ._000_add_001sub_010or_011tohi(controller_1__000_add_001sub_010or_011tohi), .opcode(Instr[31:26]),
    .funct(Instr[5:0]), .NpcSel(controller_1_npcsel), .RegDst(controller_1_regdst), .RFWrEn(RegWrite),
    ._00_zero_ext_01_sign_ext_10_move_to_hi(controller_1__00_zero_ext_01_sign_ext_10_move_to_hi),
    .DMWrEn(MemWrite), .DtoRF(controller_1_dtorf), .AluSrc(controller_1_alusrc), .alu_equal(alu_1_equal));
  // Probe on rf_1_oa
  // Probe on MemData
  Multiplexer #(.width(32), .enable("false")) multiplexer_2 (
    .in0(MemData), .in1(ext_1_out_3), .out(multiplexer_2_out), .sel(controller_1_alusrc));
  // Probe on controller_1__000_add_001sub_010or_011tohi
  ALU alu_1 (
    .A(rf_1_oa), .B(multiplexer_2_out), .O({alu_1_o[31:7], MemAddr, alu_1_o[1:0]}), .equal(alu_1_equal),
    .ALUctr(controller_1__000_add_001sub_010or_011tohi));
  Multiplexer #(.width(32), .enable("false")) multiplexer_3 (
    .in0({alu_1_o[31:7], MemAddr, alu_1_o[1:0]}), .in1(ram_1_data), .out(RegData), .sel(controller_1_dtorf));
  // Probe on {alu_1_o[31:7], MemAddr, alu_1_o[1:0]}
  RAM #(.addrWidth(5), .dataWidth(32), .bus("separate")) ram_1 (
    .addr(MemAddr), .din(MemData), .data(ram_1_data), .str(MemWrite), .clk(clk), .ld(1'b1), .clr(Reset));  // open: sel

  // Notes on the sheet:
  //   imm
  //   rs
  //   rt
  //   rd
  //   EXTop
  //   ALUsrc
  //   memout
  //   DMWE
endmodule

module IFU (
  input  clk,
  input  reset,
  input  [31:0] offset,
  input  NpcSel,
  output [31:0] out_5,
  output [31:0] instr
);

  wire and_1_out, undriven;
  wire [31:0] adder_1_out, adder_2_out, NPC, shifter_1_out;

  and and_1 (and_1_out, clk, reset);
  Register #(.width(32)) PC (.D(NPC), .Q(out_5), .clk(clk), .clr(and_1_out));  // open: en
  // Probe on undriven
  Shifter #(.width(32)) shifter_1 (.in(offset), .\dist (5'b00010), .out(shifter_1_out));
  Adder #(.width(32)) adder_1 (.a(out_5), .b(32'h4), .out(adder_1_out));  // open: cin, cout
  Adder #(.width(32)) adder_2 (.a(adder_1_out), .b(shifter_1_out), .out(adder_2_out));  // open: cin, cout
  ROM #(.addrWidth(5), .dataWidth(32)) rom_1 (.addr(out_5[6:2]), .data(instr));  // open: sel
  Multiplexer #(.width(32), .enable("false")) multiplexer_1 (
    .in0(adder_1_out), .in1(adder_2_out), .out(NPC), .sel(NpcSel));
  // Probe on NPC

  // Notes on the sheet:
  //   IM
  //   contents of rom_1 (hex, n*v repeats v):
  //   0 34210001 34428000 34437fff 222021 412823 3c060fff 3c06ffff 34e70004 ace10000 ace20004 ace3fffc
  //   8ce10000 8ce20004 8ce3fffc 35080001 35290002 10200003 34212333 10000001 34210001 210821 1284823
  //   1128fffd
endmodule

module RF (
  input  [4:0] A3,
  input  [4:0] A1,
  input  [4:0] A2,
  input  [31:0] WD,
  input  clk,
  input  reset,
  input  WE,
  output [31:0] OA,
  output [31:0] OB
);

  wire _1, _2, _3, _4, _5, _6, _7, _8, _9, _10, _11, _12, _13, _14, _15, _16, _17, _18, _19, _20, _21, _22,
       _23, _24, _25, _26, _27, _28, _29, _30, _31, and_1_out, undriven;
  wire [31:0] O1, O2, O3, O4, O5, O6, O7, O8, O9, O10, O11, O12, O13, O14, O15, O16, O17, O18, O19, O20, O21,
       O22, O23, O24, O25, O26, O27, O28, O29, O30, O31;

  Register #(.width(32)) u__1 (.D(WD), .en(_1), .Q(O1), .clk(clk), .clr(and_1_out));
  Register #(.width(32)) u__11 (.D(WD), .en(_11), .Q(O11), .clk(clk), .clr(and_1_out));
  Register #(.width(32)) u__21 (.D(WD), .en(_21), .Q(O21), .clk(clk), .clr(and_1_out));
  and and_1 (and_1_out, clk, reset);
  Demultiplexer #(.select(5)) demultiplexer_1 (
    .out1(_1), .out2(_2), .out3(_3), .out4(_4), .out5(_5), .out6(_6), .out7(_7), .out8(_8), .out9(_9),
    .out10(_10), .out11(_11), .out12(_12), .out13(_13), .out14(_14), .out15(_15), .out16(_16), .out17(_17),
    .out18(_18), .out19(_19), .out20(_20), .out21(_21), .out22(_22), .out23(_23), .out24(_24), .out25(_25),
    .out26(_26), .out27(_27), .out28(_28), .out29(_29), .out30(_30), .out31(_31), .in(WE), .sel(A3));  // open: out0, en
  // Probe on nothing
  Register #(.width(32)) u__2 (.D(WD), .en(_2), .Q(O2), .clk(clk), .clr(and_1_out));
  Register #(.width(32)) u__12 (.D(WD), .en(_12), .Q(O12), .clk(clk), .clr(and_1_out));
  Register #(.width(32)) u__22 (.D(WD), .en(_22), .Q(O22), .clk(clk), .clr(and_1_out));
  Register #(.width(32)) u__3 (.D(WD), .en(_3), .Q(O3), .clk(clk), .clr(and_1_out));
  Register #(.width(32)) u__13 (.D(WD), .en(_13), .Q(O13), .clk(clk), .clr(and_1_out));
  Register #(.width(32)) u__23 (.D(WD), .en(_23), .Q(O23), .clk(clk), .clr(and_1_out));
  Multiplexer #(.select(5), .width(32), .enable("false")) multiplexer_1 (
    .in0({32{1'b0}}), .in1(O1), .in2(O2), .in3(O3), .in4(O4), .in5(O5), .in6(O6), .in7(O7), .in8(O8),
    .in9(O9), .in10(O10), .in11(O11), .in12(O12), .in13(O13), .in14(O14), .in15(O15), .in16(O16), .in17(O17),
    .in18(O18), .in19(O19), .in20(O20), .in21(O21), .in22(O22), .in23(O23), .in24(O24), .in25(O25),
    .in26(O26), .in27(O27), .in28(O28), .in29(O29), .in30(O30), .in31(O31), .out(OA), .sel(A1));
  // Probe on undriven
  Register #(.width(32)) u__4 (.D(WD), .en(_4), .Q(O4), .clk(clk), .clr(and_1_out));
  Register #(.width(32)) u__14 (.D(WD), .en(_14), .Q(O14), .clk(clk), .clr(and_1_out));
  Register #(.width(32)) u__24 (.D(WD), .en(_24), .Q(O24), .clk(clk), .clr(and_1_out));
  Multiplexer #(.select(5), .width(32), .disabled(0), .enable("false")) multiplexer_2 (
    .in0({32{1'b0}}), .in1(O1), .in2(O2), .in3(O3), .in4(O4), .in5(O5), .in6(O6), .in7(O7), .in8(O8),
    .in9(O9), .in10(O10), .in11(O11), .in12(O12), .in13(O13), .in14(O14), .in15(O15), .in16(O16), .in17(O17),
    .in18(O18), .in19(O19), .in20(O20), .in21(O21), .in22(O22), .in23(O23), .in24(O24), .in25(O25),
    .in26(O26), .in27(O27), .in28(O28), .in29(O29), .in30(O30), .in31(O31), .out(OB), .sel(A2));
  Register #(.width(32)) u__5 (.D(WD), .en(_5), .Q(O5), .clk(clk), .clr(and_1_out));
  Register #(.width(32)) u__15 (.D(WD), .en(_15), .Q(O15), .clk(clk), .clr(and_1_out));
  Register #(.width(32)) u__25 (.D(WD), .en(_25), .Q(O25), .clk(clk), .clr(and_1_out));
  Register #(.width(32)) u__6 (.D(WD), .en(_6), .Q(O6), .clk(clk), .clr(and_1_out));
  Register #(.width(32)) u__16 (.D(WD), .en(_16), .Q(O16), .clk(clk), .clr(and_1_out));
  Register #(.width(32)) u__26 (.D(WD), .en(_26), .Q(O26), .clk(clk), .clr(and_1_out));
  Register #(.width(32)) u__7 (.D(WD), .en(_7), .Q(O7), .clk(clk), .clr(and_1_out));
  Register #(.width(32)) u__17 (.D(WD), .en(_17), .Q(O17), .clk(clk), .clr(and_1_out));
  Register #(.width(32)) u__27 (.D(WD), .en(_27), .Q(O27), .clk(clk), .clr(and_1_out));
  // Probe on O1
  // Probe on O2
  // Probe on O3
  // Probe on O4
  // Probe on O5
  // Probe on O6
  // Probe on O7
  // Probe on O8
  // Probe on O9
  // Probe on O10
  // Probe on O11
  // Probe on O12
  // Probe on O13
  // Probe on O14
  // Probe on O15
  // Probe on O16
  // Probe on O17
  // Probe on O18
  // Probe on O19
  Register #(.width(32)) u__8 (.D(WD), .en(_8), .Q(O8), .clk(clk), .clr(and_1_out));
  Register #(.width(32)) u__18 (.D(WD), .en(_18), .Q(O18), .clk(clk), .clr(and_1_out));
  Register #(.width(32)) u__28 (.D(WD), .en(_28), .Q(O28), .clk(clk), .clr(and_1_out));
  Register #(.width(32)) u__9 (.D(WD), .en(_9), .Q(O9), .clk(clk), .clr(and_1_out));
  Register #(.width(32)) u__19 (.D(WD), .en(_19), .Q(O19), .clk(clk), .clr(and_1_out));
  Register #(.width(32)) u__29 (.D(WD), .en(_29), .Q(O29), .clk(clk), .clr(and_1_out));
  Register #(.width(32)) u__10 (.D(WD), .en(_10), .Q(O10), .clk(clk), .clr(and_1_out));
  Register #(.width(32)) u__20 (.D(WD), .en(_20), .Q(O20), .clk(clk), .clr(and_1_out));
  Register #(.width(32)) u__30 (.D(WD), .en(_30), .Q(O30), .clk(clk), .clr(and_1_out));
  Register #(.width(32)) u__31 (.D(WD), .en(_31), .Q(O31), .clk(clk), .clr(and_1_out));
  // Probe on O20
  // Probe on O21
  // Probe on O22
  // Probe on O23
  // Probe on O24
  // Probe on O25
  // Probe on O26
  // Probe on O27
  // Probe on O28
  // Probe on O29
  // Probe on O30
  // Probe on O31

  // Other names for the same wires on the sheet: RA[4:0] = A1; RB[4:0] = A2; RW[4:0] = A3
endmodule

module ALU (
  input  [31:0] A,
  input  [31:0] B,
  input  [2:0] ALUctr,
  output [31:0] O,
  output equal
);

  wire [31:0] ADD, OR, SUB;

  Adder #(.width(32)) adder_1 (.a(A), .b(B), .out(ADD));  // open: cin, cout
  Subtractor #(.width(32)) subtractor_1 (.a(A), .b(B), .out(SUB));  // open: bin, bout
  assign OR = A | B;  // OR_Gate or_1, 32 bits wide
  Comparator #(.width(32)) comparator_1 (.a(A), .b(B), .eq(equal));  // open: gt, lt
  Multiplexer #(.select(3), .width(32)) multiplexer_1 (
    .in0(ADD), .in1(SUB), .in2(OR), .in3(B), .in4(A), .out(O), .sel(ALUctr));  // open: in5, in6, in7, en
endmodule

module Controller (
  input  [5:0] opcode,
  input  [5:0] funct,
  input  alu_equal,
  output [1:0] _00_zero_ext_01_sign_ext_10_move_to_hi,
  output NpcSel,
  output RegDst,
  output RFWrEn,
  output DMWrEn,
  output DtoRF,
  output AluSrc,
  output [2:0] _000_add_001sub_010or_011tohi
);

  wire add, beq, not_1_out, not_2_out, not_3_out, not_4_out, not_5_out, not_6_out, not_7_out, not_8_out,
       not_9_out, not_10_out, not_11_out, not_12_out, ori, sub;

  not not_1 (not_1_out, opcode[2]);
  not not_2 (not_2_out, opcode[5]);
  not not_3 (not_3_out, opcode[3]);
  not not_4 (not_4_out, opcode[4]);
  not not_5 (not_5_out, opcode[0]);
  not not_6 (not_6_out, opcode[1]);
  not not_7 (not_7_out, funct[4]);
  not not_8 (not_8_out, funct[3]);
  not not_9 (not_9_out, funct[5]);
  not not_10 (not_10_out, funct[2]);
  not not_11 (not_11_out, funct[0]);
  not not_12 (not_12_out, funct[1]);
  and u_add (add, not_5_out, not_6_out, not_1_out, not_3_out, not_4_out, not_2_out, funct[0], not_12_out, not_10_out, not_8_out, not_7_out, funct[5]);
  and u_sub (sub, not_5_out, not_6_out, not_1_out, not_3_out, not_4_out, not_2_out, funct[0], funct[1], not_10_out, not_8_out, not_7_out, funct[5]);
  and u_ori (ori, opcode[0], not_6_out, opcode[2], opcode[3], not_4_out, not_2_out);
  and lui (_00_zero_ext_01_sign_ext_10_move_to_hi[1], opcode[0], opcode[1], opcode[2], opcode[3], not_4_out, not_2_out);
  and lw (DtoRF, opcode[0], opcode[1], not_1_out, not_3_out, not_4_out, opcode[5]);
  and sw (DMWrEn, opcode[0], opcode[1], not_1_out, opcode[3], not_4_out, opcode[5]);
  and u_beq (beq, not_5_out, not_6_out, opcode[2], not_3_out, not_4_out, not_2_out);
  and and_1 (NpcSel, beq, alu_equal);
  or or_1 (RegDst, add, sub);
  or or_2 (RFWrEn, add, sub, ori, _00_zero_ext_01_sign_ext_10_move_to_hi[1], DtoRF);
  or or_3 (AluSrc, ori, _00_zero_ext_01_sign_ext_10_move_to_hi[1], DtoRF, DMWrEn);
  or or_4 (_000_add_001sub_010or_011tohi[1], ori, _00_zero_ext_01_sign_ext_10_move_to_hi[1]);
  or or_5 (_000_add_001sub_010or_011tohi[0], sub, _00_zero_ext_01_sign_ext_10_move_to_hi[1], beq);
  or or_6 (_00_zero_ext_01_sign_ext_10_move_to_hi[0], DtoRF, DMWrEn, beq);

  assign _000_add_001sub_010or_011tohi[2] = 1'b0;

  // Other names for the same wires on the sheet: lui = _00_zero_ext_01_sign_ext_10_move_to_hi[1]; lw = DtoRF;
  //   sw = DMWrEn
endmodule

module EXT (
  input  [1:0] _0_zero_1_sign,
  input  [15:0] in_2,
  output [31:0] out_3
);

  wire [31:0] bit_extender_1_out, bit_extender_2_out;

  assign bit_extender_1_out = {{16{1'b0}}, in_2};  // Bit_Extender bit_extender_1
  assign bit_extender_2_out = {{16{in_2[15]}}, in_2};  // Bit_Extender bit_extender_2
  Multiplexer #(.select(2), .width(32), .enable("false")) multiplexer_1 (
    .in0(bit_extender_1_out), .in1(bit_extender_2_out), .in2({in_2, {16{1'b0}}}), .out(out_3),
    .sel(_0_zero_1_sign));  // open: in3
endmodule
